# Fritzing sketch FTDI_Arduino_Mini (saved by Fritzing 0.9.9b)

parts:
  Part1 = Arduino Pro Mini v13
  Part2 = Adafruit FTDI Friend [part_number="Adafruit #284"]

nets:
  N1: Part1.DTR, Part2.RTS/DTR
  N2: Part1.D0/TX, Part2.RX
  N3: Part1.D1/RX, Part2.TX
  VCC: Part1.VCC, Part2.VCC
  GND: Part1.GND, Part2.GND, Part2.CTS

custom parts:
  Adafruit FTDI Friend: Long gone are the days of parallel ports and serial ports. Now the USB port reigns supreme! But USB is hard, and you just want to transfer your every-day serial data from a microcontroller to computer. What now? Enter the FTDI Friend! The FTDI Friend is a tweaked out FTDI FT232RL chip adapter. Sure, like the well-known FTDI cable, it can provide power to your project and there are 4 signal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
